// Logisim project Κύκλωμα 1ης Άσκηση Εργαστηρίου.circ as structural Verilog: 1 circuit, main circuit main
module main (
  input  D0,
  input  D1,
  input  D2,
  input  D3,
  input  D4,
  input  D5,
  output Y,
  output W
);

  wire and_1_out, nand_1_out, xor_1_out;

  and and_1 (and_1_out, D1, D2);
  xor xor_1 (xor_1_out, D3, D4);
  nand nand_1 (nand_1_out, D0, D2, D4);
  or or_1 (Y, nand_1_out, and_1_out, xor_1_out);
  and and_2 (W, xor_1_out, D5);
endmodule
