// Logisim project Κύκλωμα 2ης άσκησης εργαστηρίου.circ as structural Verilog: 3 circuits, main circuit FULL ADDER-SUBTRACTOR 4-BIT
module FULL_ADDER_SUBTRACTOR_4_BIT (
  input  M,
  input  A0,
  input  B0,
  input  A1,
  input  B1,
  input  A2,
  input  B2,
  input  A3,
  input  B3,
  output F0,
  output F1,
  output F2,
  output F3,
  output Z
);

  wire full_adder_1_cout, full_adder_2_cout, full_adder_3_cout, full_adder_4_cout, xor_1_out, xor_2_out,
       xor_3_out, xor_4_out;

  xor xor_1 (xor_1_out, M, B0);
  xor xor_2 (xor_2_out, M, B1);
  xor xor_3 (xor_3_out, M, B2);
  xor xor_4 (xor_4_out, M, B3);
  Full_Adder full_adder_1 (.in_1(M), .in_2(A0), .in_3(xor_1_out), .S(F0), .Cout(full_adder_1_cout));
  Full_Adder full_adder_2 (.in_1(full_adder_1_cout), .in_2(A1), .in_3(xor_2_out), .S(F1), .Cout(full_adder_2_cout));
  Full_Adder full_adder_3 (.in_1(full_adder_2_cout), .in_2(A2), .in_3(xor_3_out), .S(F2), .Cout(full_adder_3_cout));
  Full_Adder full_adder_4 (.in_1(full_adder_3_cout), .in_2(A3), .in_3(xor_4_out), .S(F3), .Cout(full_adder_4_cout));
  xor xor_5 (Z, F3, full_adder_4_cout);

  // Notes on the sheet:
  //   if(M==1) subtract 
  //   else add
  //   FA
  //   FA
  //   FA
  //   FA
  //   C0
  //   C1
  //   C2
  //   C3
endmodule

module Full_Adder (
  input  in_1,
  input  in_2,
  input  in_3,
  output S,
  output Cout
);

  wire half_adder_1_cout, half_adder_1_sum, half_adder_2_cout;

  Half_Adder half_adder_1 (.a(in_1), .b(in_2), .Sum(half_adder_1_sum), .Cout(half_adder_1_cout));
  Half_Adder half_adder_2 (.a(half_adder_1_sum), .b(in_3), .Sum(S), .Cout(half_adder_2_cout));
  or or_1 (Cout, half_adder_2_cout, half_adder_1_cout);
endmodule

module Half_Adder (
  input  a,
  input  b,
  output Sum,
  output Cout
);

  xor xor_1 (Sum, a, b);
  and and_1 (Cout, a, b);
endmodule
