// Logisim project 1)Δυαδικός πολλαπλασιαστής 4x4.circ as structural Verilog: 4 circuits, main circuit FULL ADDER 4-BIT
module FULL_ADDER_4_BIT (
  input  in_1,
  input  A0,
  input  B0,
  input  A1,
  input  B1,
  input  A2,
  input  B2,
  input  A3,
  input  B3,
  output F0,
  output F1,
  output F2,
  output F3,
  output C3
);

  wire full_adder_1_cout, full_adder_2_cout, full_adder_3_cout, xor_1_out, xor_2_out, xor_3_out, xor_4_out;

  xor xor_1 (xor_1_out, in_1, B0);
  xor xor_2 (xor_2_out, in_1, B1);
  xor xor_3 (xor_3_out, in_1, B2);
  xor xor_4 (xor_4_out, in_1, B3);
  Full_Adder full_adder_1 (.in_1(in_1), .in_2(A0), .in_3(xor_1_out), .S(F0), .Cout(full_adder_1_cout));
  Full_Adder full_adder_2 (.in_1(full_adder_1_cout), .in_2(A1), .in_3(xor_2_out), .S(F1), .Cout(full_adder_2_cout));
  Full_Adder full_adder_3 (.in_1(full_adder_2_cout), .in_2(A2), .in_3(xor_3_out), .S(F2), .Cout(full_adder_3_cout));
  Full_Adder full_adder_4 (.in_1(full_adder_3_cout), .in_2(A3), .in_3(xor_4_out), .S(F3), .Cout(C3));

  // Notes on the sheet:
  //   FA
  //   FA
  //   FA
  //   FA
  //   C0
  //   C1
  //   C2
  //   C3
endmodule

module Full_Adder (
  input  in_1,
  input  in_2,
  input  in_3,
  output S,
  output Cout
);

  wire half_adder_1_cout, half_adder_1_sum, half_adder_2_cout;

  Half_Adder half_adder_1 (.a(in_1), .b(in_2), .Sum(half_adder_1_sum), .Cout(half_adder_1_cout));
  Half_Adder half_adder_2 (.a(half_adder_1_sum), .b(in_3), .Sum(S), .Cout(half_adder_2_cout));
  or or_1 (Cout, half_adder_2_cout, half_adder_1_cout);
endmodule

module Half_Adder (
  input  a,
  input  b,
  output Sum,
  output Cout
);

  xor xor_1 (Sum, a, b);
  and and_1 (Cout, a, b);
endmodule

module \Δυαδικός_Πολλαπλασιαστής_4_Bit  (
  input  B0,
  input  \_0_για_πρόσθεση ,
  input  B1,
  input  B2,
  input  \_0_για_πρόσθεση_2 ,
  input  in_6,
  input  B3,
  input  \_0_για_πρόσθεση_3 ,
  input  A0,
  input  A1,
  input  A2,
  input  A3,
  output C0,
  output C1,
  output C2,
  output C3,
  output C4,
  output C5,
  output C6,
  output C7
);

  wire and_2_out, and_3_out, and_4_out, and_5_out, and_6_out, and_7_out, and_8_out, and_9_out, and_10_out,
       and_11_out, and_12_out, and_13_out, and_14_out, and_15_out, and_16_out, full_adder_4_bit_1_c3,
       full_adder_4_bit_1_f1, full_adder_4_bit_1_f2, full_adder_4_bit_1_f3, full_adder_4_bit_2_c3,
       full_adder_4_bit_2_f1, full_adder_4_bit_2_f2, full_adder_4_bit_2_f3;

  and and_1 (C0, B0, A0);
  and and_2 (and_2_out, B1, A0);
  and and_3 (and_3_out, B2, A0);
  and and_4 (and_4_out, B3, A0);
  and and_5 (and_5_out, B0, A1);
  and and_6 (and_6_out, B1, A1);
  and and_7 (and_7_out, B2, A1);
  and and_8 (and_8_out, B3, A1);
  and and_9 (and_9_out, B0, A2);
  and and_10 (and_10_out, B1, A2);
  and and_11 (and_11_out, B2, A2);
  and and_12 (and_12_out, B3, A2);
  and and_13 (and_13_out, B0, A3);
  and and_14 (and_14_out, B1, A3);
  and and_15 (and_15_out, B2, A3);
  and and_16 (and_16_out, B3, A3);
  FULL_ADDER_4_BIT full_adder_4_bit_1 (
    .A0(and_2_out), .B0(and_5_out), .A1(and_3_out), .B1(and_6_out), .A2(and_4_out), .B2(and_7_out),
    .A3(in_6), .B3(and_8_out), .F0(C1), .F1(full_adder_4_bit_1_f1), .F2(full_adder_4_bit_1_f2),
    .F3(full_adder_4_bit_1_f3), .C3(full_adder_4_bit_1_c3), .in_1(\_0_για_πρόσθεση ));
  FULL_ADDER_4_BIT full_adder_4_bit_2 (
    .A0(full_adder_4_bit_1_f1), .B0(and_9_out), .A1(full_adder_4_bit_1_f2), .B1(and_10_out),
    .A2(full_adder_4_bit_1_f3), .B2(and_11_out), .A3(full_adder_4_bit_1_c3), .B3(and_12_out), .F0(C2),
    .F1(full_adder_4_bit_2_f1), .F2(full_adder_4_bit_2_f2), .F3(full_adder_4_bit_2_f3),
    .C3(full_adder_4_bit_2_c3), .in_1(\_0_για_πρόσθεση_2 ));
  FULL_ADDER_4_BIT full_adder_4_bit_3 (
    .A0(full_adder_4_bit_2_f1), .B0(and_13_out), .A1(full_adder_4_bit_2_f2), .B1(and_14_out),
    .A2(full_adder_4_bit_2_f3), .B2(and_15_out), .A3(full_adder_4_bit_2_c3), .B3(and_16_out), .F0(C3),
    .F1(C4), .F2(C5), .F3(C6), .C3(C7), .in_1(\_0_για_πρόσθεση_3 ));

  // Notes on the sheet:
  //   0 γιατι δεν έχει 4 Βιτ
  //   F A-S 4Bit
  //   F A-S 4Bit
  //   F A-S 4Bit
  //   F A-S 4Bit
endmodule
