// Logisim project 2)δυαδικός συγκριτής 4x4.circ as structural Verilog: 1 circuit, main circuit main
module main (
  input  a3,
  input  b3,
  input  a2,
  input  b2,
  input  a1,
  input  b1,
  input  a0,
  input  b0,
  output a_b,
  output b_a,
  output a_b_2
);

  wire and_1_out, and_2_out, and_3_out, and_4_out, and_5_out, and_6_out, and_7_out, and_8_out, and_9_out,
       and_10_out, and_11_out, and_12_out, and_13_out, and_14_out, nor_1_out, nor_2_out, nor_3_out,
       nor_4_out, not_1_out, not_2_out, not_3_out, not_4_out, not_5_out, not_6_out, not_7_out, not_8_out;

  not not_1 (not_1_out, a3);
  not not_2 (not_2_out, b3);
  not not_3 (not_3_out, a2);
  not not_4 (not_4_out, b2);
  not not_5 (not_5_out, a1);
  not not_6 (not_6_out, b1);
  not not_7 (not_7_out, a0);
  not not_8 (not_8_out, b0);
  and and_1 (and_1_out, not_6_out, a1);
  and and_2 (and_2_out, b1, not_5_out);
  and and_3 (and_3_out, not_8_out, a0);
  and and_4 (and_4_out, b0, not_7_out);
  and and_5 (and_5_out, not_2_out, a3);
  and and_6 (and_6_out, b3, not_1_out);
  and and_7 (and_7_out, not_4_out, a2);
  and and_8 (and_8_out, b2, not_3_out);
  nor nor_1 (nor_1_out, and_1_out, and_2_out);
  nor nor_2 (nor_2_out, and_3_out, and_4_out);
  nor nor_3 (nor_3_out, and_5_out, and_6_out);
  nor nor_4 (nor_4_out, and_7_out, and_8_out);
  and and_9 (and_9_out, nor_3_out, and_7_out);
  and and_10 (and_10_out, nor_3_out, and_8_out);
  and and_11 (and_11_out, nor_3_out, nor_4_out, and_1_out);
  and and_12 (and_12_out, nor_3_out, nor_4_out, and_2_out);
  and and_13 (and_13_out, nor_3_out, nor_4_out, nor_1_out, and_3_out);
  and and_14 (and_14_out, nor_3_out, nor_4_out, nor_1_out, and_4_out);
  and and_15 (a_b_2, nor_3_out, nor_4_out, nor_1_out, nor_2_out);
  or or_1 (a_b, and_5_out, and_9_out, and_11_out, and_13_out);
  or or_2 (b_a, and_6_out, and_10_out, and_12_out, and_14_out);

  // Notes on the sheet:
  //   b>a
  //   b>a
  //   a>b
  //   b>a
  //   a>b
  //   b>a
  //   a>b
  //   a>b
endmodule
