// Logisim project 3)Πόλυπλέκτης 2 σε 1 των 8-Bit με επιλογη και επίτρεψη.circ as structural Verilog: 1 circuit, main circuit Πολυπλέκτης 2 σε 1 των 8-bit
module \Πολυπλέκτης_2_σε_1_των_8_bit  (
  input  A0,
  input  A1,
  input  A2,
  input  A3,
  input  A4,
  input  A5,
  input  A6,
  input  A7,
  input  B0,
  input  B1,
  input  B2,
  input  B3,
  input  B4,
  input  B5,
  input  B6,
  input  B7,
  input  S,
  input  E,
  output out_19,
  output out_20,
  output out_21,
  output out_22,
  output out_23,
  output out_24,
  output out_25,
  output out_26
);

  wire and_1_out, and_2_out, and_3_out, and_4_out, and_5_out, and_6_out, and_7_out, and_8_out, and_9_out,
       and_10_out, and_11_out, and_12_out, and_13_out, and_14_out, and_15_out, and_16_out, not_1_out,
       not_2_out;

  not not_1 (not_1_out, S);
  not not_2 (not_2_out, E);
  and and_1 (and_1_out, A0, not_1_out, not_2_out);
  and and_2 (and_2_out, A1, not_1_out, not_2_out);
  and and_3 (and_3_out, A2, not_1_out, not_2_out);
  and and_4 (and_4_out, A3, not_1_out, not_2_out);
  and and_5 (and_5_out, A4, not_1_out, not_2_out);
  and and_6 (and_6_out, A5, not_1_out, not_2_out);
  and and_7 (and_7_out, A6, not_1_out, not_2_out);
  and and_8 (and_8_out, A7, not_1_out, not_2_out);
  and and_9 (and_9_out, B0, S, not_2_out);
  and and_10 (and_10_out, B1, S, not_2_out);
  and and_11 (and_11_out, B2, S, not_2_out);
  and and_12 (and_12_out, B3, S, not_2_out);
  and and_13 (and_13_out, B4, S, not_2_out);
  and and_14 (and_14_out, B5, S, not_2_out);
  and and_15 (and_15_out, B6, S, not_2_out);
  and and_16 (and_16_out, B7, S, not_2_out);
  or or_1 (out_19, and_1_out, and_9_out);
  or or_2 (out_20, and_2_out, and_10_out);
  or or_3 (out_21, and_3_out, and_11_out);
  or or_4 (out_22, and_4_out, and_12_out);
  or or_5 (out_23, and_5_out, and_13_out);
  or or_6 (out_24, and_6_out, and_14_out);
  or or_7 (out_25, and_7_out, and_15_out);
  or or_8 (out_26, and_8_out, and_16_out);

  // Notes on the sheet:
  //   ΕΠΙΛΟΓΗ 0=Α ΚΑΙ 1=Β
  //   ΕΠΤΙΤΡΕΨΗ
endmodule
