// Logisim project 4)Αποκωδικοποιητής 4x16.circ as structural Verilog: 2 circuits, main circuit Αποκωδικοποιητής 4x16
module \Αποκωδικοποιητής_4x16  (
  input  A0,
  input  A1,
  input  A2,
  input  A3,
  output D0,
  output D1,
  output D2,
  output D3,
  output D4,
  output D5,
  output D6,
  output D7,
  output D8,
  output D9,
  output D10,
  output D11,
  output D12,
  output D13,
  output D14,
  output D15
);

  wire not_1_out, \αποκωδικοποιητής_3x8_1_d0_a0_prime_a1_prime_a2_prime , \αποκωδικοποιητής_3x8_1_d1 ,
       \αποκωδικοποιητής_3x8_1_d2 , \αποκωδικοποιητής_3x8_1_d3 , \αποκωδικοποιητής_3x8_1_d4 ,
       \αποκωδικοποιητής_3x8_1_d5 , \αποκωδικοποιητής_3x8_1_d6 , \αποκωδικοποιητής_3x8_1_d7 ,
       \αποκωδικοποιητής_3x8_2_d0_a0_prime_a1_prime_a2_prime , \αποκωδικοποιητής_3x8_2_d1 ,
       \αποκωδικοποιητής_3x8_2_d2 , \αποκωδικοποιητής_3x8_2_d3 , \αποκωδικοποιητής_3x8_2_d4 ,
       \αποκωδικοποιητής_3x8_2_d5 , \αποκωδικοποιητής_3x8_2_d6 , \αποκωδικοποιητής_3x8_2_d7 ;

  not not_1 (not_1_out, A3);
  \Αποκωδικοποιητής_3x8  \u_αποκωδικοποιητής_3x8_1  (
    .A0(A0), .A1(A1), .A2(A2),
    .D0_a0_prime_a1_prime_a2_prime(\αποκωδικοποιητής_3x8_1_d0_a0_prime_a1_prime_a2_prime ),
    .D1(\αποκωδικοποιητής_3x8_1_d1 ), .D2(\αποκωδικοποιητής_3x8_1_d2 ), .D3(\αποκωδικοποιητής_3x8_1_d3 ),
    .D4(\αποκωδικοποιητής_3x8_1_d4 ), .D5(\αποκωδικοποιητής_3x8_1_d5 ), .D6(\αποκωδικοποιητής_3x8_1_d6 ),
    .D7(\αποκωδικοποιητής_3x8_1_d7 ));
  \Αποκωδικοποιητής_3x8  \u_αποκωδικοποιητής_3x8_2  (
    .A0(A0), .A1(A1), .A2(A2),
    .D0_a0_prime_a1_prime_a2_prime(\αποκωδικοποιητής_3x8_2_d0_a0_prime_a1_prime_a2_prime ),
    .D1(\αποκωδικοποιητής_3x8_2_d1 ), .D2(\αποκωδικοποιητής_3x8_2_d2 ), .D3(\αποκωδικοποιητής_3x8_2_d3 ),
    .D4(\αποκωδικοποιητής_3x8_2_d4 ), .D5(\αποκωδικοποιητής_3x8_2_d5 ), .D6(\αποκωδικοποιητής_3x8_2_d6 ),
    .D7(\αποκωδικοποιητής_3x8_2_d7 ));
  and and_1 (D0, \αποκωδικοποιητής_3x8_1_d0_a0_prime_a1_prime_a2_prime , not_1_out);
  and and_2 (D1, \αποκωδικοποιητής_3x8_1_d1 , not_1_out);
  and and_3 (D2, \αποκωδικοποιητής_3x8_1_d2 , not_1_out);
  and and_4 (D3, \αποκωδικοποιητής_3x8_1_d3 , not_1_out);
  and and_5 (D4, \αποκωδικοποιητής_3x8_1_d4 , not_1_out);
  and and_6 (D5, \αποκωδικοποιητής_3x8_1_d5 , not_1_out);
  and and_7 (D6, \αποκωδικοποιητής_3x8_1_d6 , not_1_out);
  and and_8 (D7, \αποκωδικοποιητής_3x8_1_d7 , not_1_out);
  and and_9 (D8, \αποκωδικοποιητής_3x8_2_d0_a0_prime_a1_prime_a2_prime , A3);
  and and_10 (D9, \αποκωδικοποιητής_3x8_2_d1 , A3);
  and and_11 (D10, \αποκωδικοποιητής_3x8_2_d2 , A3);
  and and_12 (D11, \αποκωδικοποιητής_3x8_2_d3 , A3);
  and and_13 (D12, \αποκωδικοποιητής_3x8_2_d4 , A3);
  and and_14 (D13, \αποκωδικοποιητής_3x8_2_d5 , A3);
  and and_15 (D14, \αποκωδικοποιητής_3x8_2_d6 , A3);
  and and_16 (D15, \αποκωδικοποιητής_3x8_2_d7 , A3);

  // Notes on the sheet:
  //   Αποκωδικοποιητής 3Χ8
  //   Αποκωδικοποιητής 3Χ8
endmodule

module \Αποκωδικοποιητής_3x8  (
  input  A0,
  input  A1,
  input  A2,
  output D0_a0_prime_a1_prime_a2_prime,
  output D1,
  output D2,
  output D3,
  output D4,
  output D5,
  output D6,
  output D7
);

  wire not_1_out, not_2_out, not_3_out;

  not not_1 (not_1_out, A0);
  not not_2 (not_2_out, A1);
  not not_3 (not_3_out, A2);
  and and_1 (D0_a0_prime_a1_prime_a2_prime, not_1_out, not_2_out, not_3_out);
  and and_2 (D1, A0, not_2_out, not_3_out);
  and and_3 (D2, not_1_out, A1, not_3_out);
  and and_4 (D3, A0, A1, not_3_out);
  and and_5 (D4, not_1_out, not_2_out, A2);
  and and_6 (D5, A0, not_2_out, A2);
  and and_7 (D6, not_1_out, A1, A2);
  and and_8 (D7, A0, A1, A2);

  // Notes on the sheet:
  //   Αποκωδικοποιητής 3Χ8
endmodule
