// Logisim project Κυκλώματα 4ης εργαστηριακής άσκησης.circ as structural Verilog: 3 circuits, main circuit jk flip-flop
module \καταχωρητής_ολίσθησης_4_Βιτ  (
  input  Control,
  input  CLK,
  input  D,
  input  Preset,
  input  Clear,
  output Q
);

  wire and_1_out, d_ff_1_q, d_ff_2_q, d_ff_3_q;

  and and_1 (and_1_out, Control, CLK);
  D_Flip_Flop d_ff_1 (.clk(and_1_out), .D(D), .Q(d_ff_1_q), .preset(Preset), .reset(Clear));  // open: Qn, en
  LED led_1 (.in(d_ff_1_q));
  LED led_2 (.in(d_ff_2_q));
  D_Flip_Flop d_ff_2 (.clk(and_1_out), .D(d_ff_1_q), .Q(d_ff_2_q), .preset(Preset), .reset(Clear));  // open: Qn, en
  D_Flip_Flop d_ff_3 (.clk(and_1_out), .D(d_ff_2_q), .Q(d_ff_3_q), .preset(Preset), .reset(Clear));  // open: Qn, en
  LED led_3 (.in(d_ff_3_q));
  LED led_4 (.in(Q));
  D_Flip_Flop d_ff_4 (.clk(and_1_out), .D(d_ff_3_q), .Q(Q), .preset(Preset), .reset(Clear));  // open: Qn, en
endmodule

module jk_flip_flop (
  input  J,
  input  K,
  input  CLK,
  input  Preset,
  input  Clear,
  output Q,
  output Q_prime
);

  wire and_1_out, and_2_out, not_1_out, or_1_out;

  not not_1 (not_1_out, K);
  and and_1 (and_1_out, Q_prime, J);
  and and_2 (and_2_out, not_1_out, Q);
  or or_1 (or_1_out, and_1_out, and_2_out);
  D_Flip_Flop d_ff_1 (.clk(or_1_out), .D(CLK), .Q(Q), .Qn(Q_prime), .preset(Preset), .reset(Clear));  // open: en
endmodule

module \αθροιστής_με_καταχωρητές_μετατόπισης  (
  input  Preset,
  input  Clear
);

  wire adder_1_cout, adder_1_out, clock_1_out, jk_flip_flop_1_q, not_1_out, shift_register_1_out,
       shift_register_2_out;

  Clock clock_1 (.out(clock_1_out));
  Shift_Register #(.length(4)) shift_register_1 (
    .in(adder_1_out), .clk(clock_1_out), .out(shift_register_1_out));  // open: shift, load, clr, d0, q0, d1, q1, d2, q2, d3, q3
  Shift_Register #(.length(4)) shift_register_2 (
    .clk(clock_1_out), .out(shift_register_2_out));  // open: shift, in, load, clr, d0, q0, d1, q1, d2, q2, d3, q3
  not not_1 (not_1_out, clock_1_out);
  jk_flip_flop jk_flip_flop_1 (
    .J(clock_1_out), .K(not_1_out), .CLK(adder_1_cout), .Q(jk_flip_flop_1_q), .Preset(Preset), .Clear(Clear));  // open: Q_prime
  Adder #(.width(1)) adder_1 (
    .a(shift_register_1_out), .b(shift_register_2_out), .out(adder_1_out), .cin(jk_flip_flop_1_q),
    .cout(adder_1_cout));
endmodule
