// Logisim project circ.circ as structural Verilog: 2 circuits, main circuit 5bit ασύγχρονος δυαδικός μετρητής JK-FF
module \_5bit_ασύγχρονος_δυαδικός_μετρητής_JK_FF  (
  input  Clear,
  output out_2,
  output out_3,
  output out_4,
  output out_5,
  output out_6
);

  wire clock_1_out, j_k_ff_1_qn, j_k_ff_2_qn, j_k_ff_3_qn, j_k_ff_4_qn, j_k_ff_5_qn, not_1_out, not_2_out,
       not_3_out, not_4_out, not_5_out;

  Clock clock_1 (.out(clock_1_out));
  not not_1 (not_1_out, j_k_ff_1_qn);
  not not_2 (not_2_out, j_k_ff_2_qn);
  not not_3 (not_3_out, j_k_ff_3_qn);
  not not_4 (not_4_out, j_k_ff_4_qn);
  not not_5 (not_5_out, j_k_ff_5_qn);
  J_K_Flip_Flop #(.trigger("falling")) j_k_ff_1 (
    .J(j_k_ff_1_qn), .clk(clock_1_out), .K(not_1_out), .Q(out_2), .Qn(j_k_ff_1_qn), .reset(Clear));  // open: preset, en
  J_K_Flip_Flop #(.trigger("falling")) j_k_ff_2 (
    .J(j_k_ff_2_qn), .clk(out_2), .K(not_2_out), .Q(out_3), .Qn(j_k_ff_2_qn), .reset(Clear));  // open: preset, en
  J_K_Flip_Flop #(.trigger("falling")) j_k_ff_3 (
    .J(j_k_ff_3_qn), .clk(out_3), .K(not_3_out), .Q(out_4), .Qn(j_k_ff_3_qn), .reset(Clear));  // open: preset, en
  J_K_Flip_Flop #(.trigger("falling")) j_k_ff_4 (
    .J(j_k_ff_4_qn), .clk(out_4), .K(not_4_out), .Q(out_5), .Qn(j_k_ff_4_qn), .reset(Clear));  // open: preset, en
  J_K_Flip_Flop #(.trigger("falling")) j_k_ff_5 (
    .J(j_k_ff_5_qn), .clk(out_5), .K(not_5_out), .Q(out_6), .Qn(j_k_ff_5_qn), .reset(Clear));  // open: preset, en
endmodule

module \_5bit_σύγχρονος_δυαδικός_μετρητής__D_FF  (
  input  Preset,
  output out_2,
  output out_3,
  output out_4,
  output out_5,
  output out_6
);

  wire and_1_out, and_2_out, and_3_out, and_4_out, and_5_out, and_6_out, and_7_out, and_8_out, clock_1_out,
       d_ff_1_qn, not_1_out, not_2_out, not_3_out, not_4_out, not_5_out, not_6_out, not_7_out, or_1_out,
       or_2_out, or_3_out, or_4_out, xor_1_out, xor_2_out;

  not not_1 (not_1_out, out_3);
  not not_2 (not_2_out, out_2);
  xor xor_1 (xor_1_out, out_4, out_2);
  not not_3 (not_3_out, out_5);
  not not_4 (not_4_out, out_4);
  not not_5 (not_5_out, out_3);
  and and_1 (and_1_out, out_3, not_2_out);
  not not_6 (not_6_out, out_6);
  and and_2 (and_2_out, out_5, out_4, out_3, out_2);
  and and_3 (and_3_out, out_3, xor_1_out);
  and and_4 (and_4_out, out_4, not_1_out);
  and and_5 (and_5_out, not_3_out, out_4, out_3, out_2);
  or or_1 (or_1_out, not_4_out, not_5_out, and_1_out);
  and and_6 (and_6_out, not_6_out, out_5, out_4, out_3, out_2);
  not not_7 (not_7_out, and_2_out);
  xor xor_2 (xor_2_out, out_3, out_2);
  and and_7 (and_7_out, out_5, or_1_out);
  and and_8 (and_8_out, out_6, not_7_out);
  or or_2 (or_2_out, and_3_out, and_4_out);
  or or_3 (or_3_out, and_6_out, and_8_out);
  Clock clock_1 (.out(clock_1_out));
  or or_4 (or_4_out, and_5_out, and_7_out);
  D_Flip_Flop #(.trigger("falling")) d_ff_1 (
    .clk(clock_1_out), .D(d_ff_1_qn), .Q(out_2), .Qn(d_ff_1_qn), .reset(Preset));  // open: preset, en
  D_Flip_Flop #(.trigger("falling")) d_ff_2 (
    .clk(clock_1_out), .D(xor_2_out), .Q(out_3), .reset(Preset));  // open: Qn, preset, en
  D_Flip_Flop #(.trigger("falling")) d_ff_3 (
    .clk(clock_1_out), .D(or_2_out), .Q(out_4), .reset(Preset));  // open: Qn, preset, en
  D_Flip_Flop d_ff_4 (.clk(clock_1_out), .D(or_4_out), .Q(out_5), .reset(Preset));  // open: Qn, preset, en
  D_Flip_Flop d_ff_5 (.clk(clock_1_out), .D(or_3_out), .Q(out_6), .reset(Preset));  // open: Qn, preset, en

  // Notes on the sheet:
  //   Q0
  //   Q1
  //   Q2
  //   Q2 xor Q0
  //   Q3
  //   Q4
  //   Q1' and Q2
  //   q3'q2q1q0
  //   q2'
  //   q1'
  //   q1q0'
  //   (q0q1q2q3)'
  //   q3(q1'+q2'+q1q0')
  //   q4'q3q2q1q0
  //   q4(q0q1q2q3)'
endmodule
