// Logisim project 6η Άσκηση.circ as structural Verilog: 3 circuits, main circuit 5bit ασύγχρονος δυαδικός αφαιρετικός  μετρητής JK-FF
module \_5bit_ασύγχρονος_δυαδικός_αφαιρετικός__μετρητής_JK_FF  (
  input  Clock,
  input  Clear,
  output out_3,
  output out_4,
  output out_5,
  output out_6,
  output out_7
);

  wire j_k_ff_1_q, j_k_ff_1_qn, j_k_ff_2_q, j_k_ff_2_qn, j_k_ff_3_q, j_k_ff_3_qn, j_k_ff_4_q, j_k_ff_4_qn,
       j_k_ff_5_q, j_k_ff_5_qn, not_1_out, not_2_out, not_3_out, not_4_out, not_5_out;

  J_K_Flip_Flop #(.trigger("falling")) j_k_ff_1 (
    .J(j_k_ff_1_qn), .clk(Clock), .K(not_1_out), .Q(j_k_ff_1_q), .Qn(j_k_ff_1_qn), .reset(Clear));  // open: preset, en
  not not_1 (not_1_out, j_k_ff_1_qn);
  J_K_Flip_Flop #(.trigger("falling")) j_k_ff_2 (
    .J(j_k_ff_2_qn), .clk(j_k_ff_1_q), .K(not_2_out), .Q(j_k_ff_2_q), .Qn(j_k_ff_2_qn), .reset(Clear));  // open: preset, en
  not not_2 (not_2_out, j_k_ff_2_qn);
  J_K_Flip_Flop #(.trigger("falling")) j_k_ff_3 (
    .J(j_k_ff_3_qn), .clk(j_k_ff_2_q), .K(not_3_out), .Q(j_k_ff_3_q), .Qn(j_k_ff_3_qn), .reset(Clear));  // open: preset, en
  not not_3 (not_3_out, j_k_ff_3_qn);
  J_K_Flip_Flop #(.trigger("falling")) j_k_ff_4 (
    .J(j_k_ff_4_qn), .clk(j_k_ff_3_q), .K(not_4_out), .Q(j_k_ff_4_q), .Qn(j_k_ff_4_qn), .reset(Clear));  // open: preset, en
  not not_4 (not_4_out, j_k_ff_4_qn);
  J_K_Flip_Flop #(.trigger("falling")) j_k_ff_5 (
    .J(j_k_ff_5_qn), .clk(j_k_ff_4_q), .K(not_5_out), .Q(j_k_ff_5_q), .Qn(j_k_ff_5_qn), .reset(Clear));  // open: preset, en
  not not_5 (not_5_out, j_k_ff_5_qn);
  not not_6 (out_3, j_k_ff_1_q);
  not not_7 (out_4, j_k_ff_2_q);
  not not_8 (out_5, j_k_ff_3_q);
  not not_9 (out_6, j_k_ff_4_q);
  not not_10 (out_7, j_k_ff_5_q);
endmodule

module \_5bit_σύγχρονος_δυαδικός_μετρητής__D_FF  (
  input  Clock,
  input  Preset,
  output out_3,
  output out_4,
  output out_5,
  output out_6,
  output out_7
);

  wire and_1_out, and_2_out, and_3_out, and_4_out, and_5_out, and_6_out, and_7_out, and_8_out, d_ff_1_qn,
       not_1_out, not_2_out, not_3_out, not_4_out, not_5_out, not_6_out, not_7_out, or_1_out, or_2_out,
       or_3_out, or_4_out, xor_1_out, xor_2_out;

  not not_1 (not_1_out, out_4);
  not not_2 (not_2_out, out_3);
  xor xor_1 (xor_1_out, out_5, out_3);
  not not_3 (not_3_out, out_6);
  not not_4 (not_4_out, out_5);
  not not_5 (not_5_out, out_4);
  and and_1 (and_1_out, out_4, not_2_out);
  not not_6 (not_6_out, out_7);
  and and_2 (and_2_out, out_6, out_5, out_4, out_3);
  and and_3 (and_3_out, out_4, xor_1_out);
  and and_4 (and_4_out, out_5, not_1_out);
  and and_5 (and_5_out, not_3_out, out_5, out_4, out_3);
  or or_1 (or_1_out, not_4_out, not_5_out, and_1_out);
  and and_6 (and_6_out, not_6_out, out_6, out_5, out_4, out_3);
  not not_7 (not_7_out, and_2_out);
  xor xor_2 (xor_2_out, out_4, out_3);
  and and_7 (and_7_out, out_6, or_1_out);
  and and_8 (and_8_out, out_7, not_7_out);
  or or_2 (or_2_out, and_3_out, and_4_out);
  or or_3 (or_3_out, and_6_out, and_8_out);
  or or_4 (or_4_out, and_5_out, and_7_out);
  D_Flip_Flop #(.trigger("falling")) d_ff_1 (
    .clk(Clock), .D(d_ff_1_qn), .Q(out_3), .Qn(d_ff_1_qn), .reset(Preset));  // open: preset, en
  D_Flip_Flop #(.trigger("falling")) d_ff_2 (
    .clk(Clock), .D(xor_2_out), .Q(out_4), .reset(Preset));  // open: Qn, preset, en
  D_Flip_Flop #(.trigger("falling")) d_ff_3 (
    .clk(Clock), .D(or_2_out), .Q(out_5), .reset(Preset));  // open: Qn, preset, en
  D_Flip_Flop d_ff_4 (.clk(Clock), .D(or_4_out), .Q(out_6), .reset(Preset));  // open: Qn, preset, en
  D_Flip_Flop d_ff_5 (.clk(Clock), .D(or_3_out), .Q(out_7), .reset(Preset));  // open: Qn, preset, en

  // Notes on the sheet:
  //   Q0
  //   Q1
  //   Q2
  //   Q2 xor Q0
  //   Q3
  //   Q4
  //   Q1' and Q2
  //   q3'q2q1q0
  //   q2'
  //   q1'
  //   q1q0'
  //   (q0q1q2q3)'
  //   q3(q1'+q2'+q1q0')
  //   q4'q3q2q1q0
  //   q4(q0q1q2q3)'
endmodule

module \έλεγχος_της__μνήμης  (
  input  mode
);

  wire button_1_out, clock_1_out, comparator_1_eq, comparator_1_gt, comparator_1_lt, not_1_out;
  wire [4:0] \n5bit_ασύγχρονος_δυαδικός_αφαιρετικός_μετρητής_jk_ff_1_out_3 ,
       \n5bit_σύγχρονος_δυαδικός_μετρητής_d_ff_1_out_3 , ram_1_data;

  Clock clock_1 (.out(clock_1_out));
  \_5bit_σύγχρονος_δυαδικός_μετρητής__D_FF  \u_5bit_σύγχρονος_δυαδικός_μετρητής_d_ff_1  (
    .out_3(\n5bit_σύγχρονος_δυαδικός_μετρητής_d_ff_1_out_3 [0]),
    .out_4(\n5bit_σύγχρονος_δυαδικός_μετρητής_d_ff_1_out_3 [1]),
    .out_5(\n5bit_σύγχρονος_δυαδικός_μετρητής_d_ff_1_out_3 [2]),
    .out_6(\n5bit_σύγχρονος_δυαδικός_μετρητής_d_ff_1_out_3 [3]),
    .out_7(\n5bit_σύγχρονος_δυαδικός_μετρητής_d_ff_1_out_3 [4]), .Clock(clock_1_out), .Preset(button_1_out));
  \_5bit_ασύγχρονος_δυαδικός_αφαιρετικός__μετρητής_JK_FF  \u_5bit_ασύγχρονος_δυαδικός_αφαιρετικός_μετρητής_jk_ff_1  (
    .Clock(clock_1_out), .Clear(button_1_out),
    .out_3(\n5bit_ασύγχρονος_δυαδικός_αφαιρετικός_μετρητής_jk_ff_1_out_3 [0]),
    .out_4(\n5bit_ασύγχρονος_δυαδικός_αφαιρετικός_μετρητής_jk_ff_1_out_3 [1]),
    .out_5(\n5bit_ασύγχρονος_δυαδικός_αφαιρετικός_μετρητής_jk_ff_1_out_3 [2]),
    .out_6(\n5bit_ασύγχρονος_δυαδικός_αφαιρετικός_μετρητής_jk_ff_1_out_3 [3]),
    .out_7(\n5bit_ασύγχρονος_δυαδικός_αφαιρετικός_μετρητής_jk_ff_1_out_3 [4]));
  not not_1 (not_1_out, mode);
  RAM #(.addrWidth(5), .dataWidth(5), .bus("separate")) ram_1 (
    .addr(\n5bit_σύγχρονος_δυαδικός_μετρητής_d_ff_1_out_3 ),
    .din(\n5bit_ασύγχρονος_δυαδικός_αφαιρετικός_μετρητής_jk_ff_1_out_3 ), .data(ram_1_data), .str(mode),
    .clk(clock_1_out), .ld(not_1_out), .clr(button_1_out));  // open: sel
  Button button_1 (.out(button_1_out));
  Comparator #(.width(5)) comparator_1 (
    .a(ram_1_data), .b(\n5bit_ασύγχρονος_δυαδικός_αφαιρετικός_μετρητής_jk_ff_1_out_3 ), .gt(comparator_1_gt),
    .eq(comparator_1_eq), .lt(comparator_1_lt));
  LED led_1 (.in(comparator_1_gt));
  LED led_2 (.in(comparator_1_eq));
  LED led_3 (.in(comparator_1_lt));

  // Notes on the sheet:
  //   if mode=0 then memory check
  //   if mode =1 then memory fill
  //   Clear
  //   ισότητα
endmodule
