// Logisim project Εργασία Εξαμήνου Ζήτημα Α'.circ as structural Verilog: 1 circuit, main circuit main
// ALU
module main (
  input  Cin,
  input  A0,
  input  B0,
  input  A1,
  input  B1,
  input  [2:0] F2_F1_F0,
  output out0,
  output out1,
  output Cout_of_A_B,
  output Cout_of_A_1
);

  wire adder_1_cout, adder_1_out, adder_2_out, adder_3_cout, adder_3_out, adder_4_out, nand_1_out,
       nand_2_out, not_1_out, not_2_out, xor_1_out, xor_2_out;

  not not_1 (not_1_out, A0);
  xor xor_1 (xor_1_out, A0, B0);
  nand nand_1 (nand_1_out, A0, B0);
  not not_2 (not_2_out, A1);
  xor xor_2 (xor_2_out, A1, B1);
  nand nand_2 (nand_2_out, A1, B1);
  Adder #(.width(1)) adder_1 (.a(A0), .b(B0), .out(adder_1_out), .cin(Cin), .cout(adder_1_cout));
  Adder #(.width(1)) adder_2 (.a(A1), .b(B1), .out(adder_2_out), .cin(adder_1_cout), .cout(Cout_of_A_B));
  Adder #(.width(1)) adder_3 (.a(A0), .b(1'b1), .out(adder_3_out), .cout(adder_3_cout));  // open: cin
  Adder #(.width(1)) adder_4 (.a(A1), .b(1'b0), .out(adder_4_out), .cin(adder_3_cout), .cout(Cout_of_A_1));
  Multiplexer #(.select(3)) multiplexer_1 (
    .in0(not_1_out), .in1(xor_1_out), .in2(nand_1_out), .in3(adder_1_out), .in4(adder_3_out), .out(out0),
    .sel(F2_F1_F0));  // open: in5, in6, in7, en
  Multiplexer #(.select(3)) multiplexer_2 (
    .in0(not_2_out), .in1(xor_2_out), .in2(nand_2_out), .in3(adder_2_out), .in4(adder_4_out), .out(out1),
    .sel(F2_F1_F0));  // open: in5, in6, in7, en

  // Notes on the sheet:
  //   Select Bits
  //   000 - Not
  //   001 - Xor
  //   010 - Nand
  //   011 - Add
  //   100 - A+1
  //   else return X
  //   Not
  //   Xor
  //   Nand
  //   Add
  //   A+1
  //   Not
  //   Xor
  //   Nand
  //   Add
  //   A+1
endmodule
