// Logisim project Εργασία Εξαμήνου Ζήτημα Β'.circ as structural Verilog: 1 circuit, main circuit main
module main (
);

  wire and_1_out, and_2_out, button_1_out, Clock_out, j_k_ff_4_qn;
  wire [3:0] j_k_ff_1_q;

  Clock Clock (.out(Clock_out));
  Button button_1 (.out(button_1_out));
  and and_1 (and_1_out, j_k_ff_1_q[1], j_k_ff_1_q[0]);
  and and_2 (and_2_out, j_k_ff_1_q[2], j_k_ff_1_q[1], j_k_ff_1_q[0]);
  J_K_Flip_Flop #(.trigger("falling")) j_k_ff_1 (
    .J(j_k_ff_4_qn), .clk(Clock_out), .K(1'b1), .Q(j_k_ff_1_q[0]), .reset(button_1_out));  // open: Qn, preset, en
  J_K_Flip_Flop #(.trigger("falling")) j_k_ff_2 (
    .J(j_k_ff_1_q[0]), .clk(Clock_out), .K(j_k_ff_1_q[0]), .Q(j_k_ff_1_q[1]), .reset(button_1_out));  // open: Qn, preset, en
  J_K_Flip_Flop #(.trigger("falling")) j_k_ff_3 (
    .J(and_1_out), .clk(Clock_out), .K(and_1_out), .Q(j_k_ff_1_q[2]), .reset(button_1_out));  // open: Qn, preset, en
  J_K_Flip_Flop #(.trigger("falling")) j_k_ff_4 (
    .J(and_2_out), .clk(Clock_out), .K(1'b1), .Q(j_k_ff_1_q[3]), .Qn(j_k_ff_4_qn), .reset(button_1_out));  // open: preset, en
  LED led_1 (.in(j_k_ff_1_q[0]));
  LED led_2 (.in(j_k_ff_1_q[1]));
  LED led_3 (.in(j_k_ff_1_q[2]));
  LED led_4 (.in(j_k_ff_1_q[3]));
  Hex_Digit_Display hex_digit_display_1 (.value(j_k_ff_1_q));  // open: dp

  // Notes on the sheet:
  //   NOT Q3
  //   Clear
  //   NOT Q3
  //   Q0
  //   Q0
  //   AND
  //   Q1
  //   Q0
  //   AND
  //   Q1
  //   AND
  //   Q2
  //   NOT Q3
  //   Q0
  //   Q2
  //   Q2
  //   Q1
  //   Q1
  //   Q1
  //   Q3
  //   Q0
  //   Q0
  //   Q0
  //   Q0
  //   Q1
  //   Q2
  //   Q3
  //   Q1
  //   Q1
  //   Q2
  //   Q2
  //   Q3
  //   Q0
  //   Q0
  //   Q3
endmodule
